// Logisim project CPU.circ as structural Verilog: 13 circuits, main circuit main2
module dataPath (
  input  wtEN,
  input  rdEN,
  input  ARinr,
  input  ARload,
  input  ARclr,
  input  PCinr,
  input  PCload,
  input  PCclr,
  input  DRinr,
  input  DRload,
  input  DRclr,
  input  [2:0] S2S1S0,
  input  ACinr,
  input  ACload,
  input  ACclr,
  input  comE,
  input  Eload,
  input  [2:0] ALUselect,
  input  Eclr,
  input  IRload,
  input  TRinr,
  input  TRload,
  input  TRclr,
  output [15:0] DR_15_0,
  output [15:0] AC_15_0,
  output Eop,
  output [15:0] IR_15_0
);

  wire alu_new_1_cout, clock_1_out;
  wire [11:0] AR_b12, b16_b12_1_out_2, b16_b12_2_out_2;
  wire [15:0] alu_new_1_aluout, AR_b16, multiplexer_1_out, PC_b16, ram_1_dout, TR_ou;

  Clock clock_1 (.out(clock_1_out));
  b16_b12 b16_b12_1 (.in_1(multiplexer_1_out), .out_2(b16_b12_1_out_2));
  b16_b12 b16_b12_2 (.in_1(multiplexer_1_out), .out_2(b16_b12_2_out_2));
  RAM #(.addrWidth(12), .asyncread("true"), .dataWidth(16)) ram_1 (
    .addr(AR_b12), .we(wtEN), .oe(rdEN), .clk(clock_1_out), .din(multiplexer_1_out), .dout(ram_1_dout));
  ar_pc_reg AR (
    .Incrementer(ARinr), .inp(b16_b12_1_out_2), .Load(ARload), .Clear(ARclr), .clk(clock_1_out),
    .b16(AR_b16), .b12(AR_b12));
  ar_pc_reg PC (
    .Incrementer(PCinr), .inp(b16_b12_2_out_2), .Load(PCload), .Clear(PCclr), .clk(clock_1_out), .b16(PC_b16));  // open: b12
  ac_dr_ir_tr_reg DR (
    .Incrementer(DRinr), .inp(multiplexer_1_out), .Load(DRload), .Clear(DRclr), .clk(clock_1_out),
    .ou(DR_15_0));
  ac_dr_ir_tr_reg AC (
    .Incrementer(ACinr), .inp(alu_new_1_aluout), .Load(ACload), .Clear(ACclr), .clk(clock_1_out), .ou(AC_15_0));
  ALU_new alu_new_1 (
    .AC(AC_15_0), .DR(DR_15_0), .ALUselect(ALUselect), .IPLS(Eop), .IPRS(Eop), .ALUout(alu_new_1_aluout),
    .Cout(alu_new_1_cout));  // open: INPR
  ac_dr_ir_tr_reg IR (
    .inp(multiplexer_1_out), .Load(IRload), .clk(clock_1_out), .ou(IR_15_0));  // open: Incrementer, Clear
  ac_dr_ir_tr_reg TR (
    .Incrementer(TRinr), .inp(multiplexer_1_out), .Load(TRload), .Clear(TRclr), .clk(clock_1_out), .ou(TR_ou));
  E_FF e_ff_1 (.E_ip(alu_new_1_cout), .comE(comE), .load(Eload), .clr(Eclr), .clk(clock_1_out), .E_ff_out(Eop));
  Multiplexer #(.select(3), .width(16)) multiplexer_1 (
    .in1(AR_b16), .in2(PC_b16), .in3(DR_15_0), .in4(AC_15_0), .in5(IR_15_0), .in6(TR_ou), .in7(ram_1_dout),
    .out(multiplexer_1_out), .sel(S2S1S0));  // open: in0

  // Other names for the same wires on the sheet: ACout[15:0] = AC_15_0; DRout[15:0] = DR_15_0; E_ff_op = Eop
endmodule

module ac_dr_ir_tr_reg (
  input  Incrementer,
  input  [15:0] inp,
  input  Load,
  input  Clear,
  input  clk,
  output [15:0] ou
);

  wire [15:0] adder_1_out, multiplexer_1_out, multiplexer_2_out, multiplexer_3_out;

  Multiplexer #(.width(16)) multiplexer_1 (.in0(ou), .in1(adder_1_out), .out(multiplexer_1_out), .sel(Incrementer));
  Multiplexer #(.width(16)) multiplexer_2 (.in0(multiplexer_1_out), .in1(inp), .out(multiplexer_2_out), .sel(Load));
  Multiplexer #(.width(16)) multiplexer_3 (
    .in0(multiplexer_2_out), .in1({16{1'b0}}), .out(multiplexer_3_out), .sel(Clear));
  Register #(.width(16)) register_1 (.D(multiplexer_3_out), .clk(clk), .Q(ou));  // open: en, clr
  Adder #(.width(16)) adder_1 (.a(16'h1), .b(ou), .out(adder_1_out), .cin(1'b0));  // open: cout
endmodule

module ar_pc_reg (
  input  Incrementer,
  input  [11:0] inp,
  input  Load,
  input  Clear,
  input  clk,
  output [15:0] b16,
  output [11:0] b12
);

  wire [11:0] adder_1_out, multiplexer_1_out, multiplexer_2_out, multiplexer_3_out;

  Multiplexer #(.width(12)) multiplexer_1 (.in0(b12), .in1(adder_1_out), .out(multiplexer_1_out), .sel(Incrementer));
  Multiplexer #(.width(12)) multiplexer_2 (.in0(multiplexer_1_out), .in1(inp), .out(multiplexer_2_out), .sel(Load));
  Multiplexer #(.width(12)) multiplexer_3 (
    .in0(multiplexer_2_out), .in1({12{1'b0}}), .out(multiplexer_3_out), .sel(Clear));
  Register #(.width(12)) register_1 (.D(multiplexer_3_out), .clk(clk), .Q(b12));  // open: en, clr
  Adder #(.width(12)) adder_1 (.a(12'h1), .b(b12), .out(adder_1_out), .cin(1'b0));  // open: cout

  assign b16 = {4'b0000, b12};
endmodule

module b16_b12 (
  input  [15:0] in_1,
  output [11:0] out_2
);


  assign out_2 = in_1[11:0];
endmodule

module ALU (
  input  [15:0] Ai,
  input  [15:0] Bi,
  input  Cin,
  input  [1:0] S0S1,
  input  [1:0] S3S2,
  output [15:0] Fi,
  output Cout
);

  wire alu_8b_2_out_6;

  ALU_8b alu_8b_1 (.A(Ai[15:8]), .S1_S0(S0S1), .S3_S2(S3S2), .B(Bi[15:8]), .out_6(Cout), .ou(Fi[15:8]));  // open: Cin
  ALU_8b alu_8b_2 (
    .A(Ai[7:0]), .S1_S0(S0S1), .S3_S2(S3S2), .Cin(Cin), .B(Bi[7:0]), .out_6(alu_8b_2_out_6), .ou(Fi[7:0]));
endmodule

module ALU_8b (
  input  [7:0] A,
  input  [1:0] S1_S0,
  input  [1:0] S3_S2,
  input  Cin,
  input  [7:0] B,
  output out_6,
  output [7:0] ou
);

  wire sub_alu_2_cout, sub_alu_3_cout, sub_alu_4_cout, sub_alu_6_cout, sub_alu_7_cout, sub_alu_8_cout;
  wire [1:0] undriven;

  sub_ALU sub_alu_1 (
    .Ai(A[7]), .Cin(sub_alu_2_cout), .Bi(B[7]), .S1_S0(undriven), .S3_S2(S3_S2), .A_i1(1'b0), .A_i2(A[6]),
    .Cout(out_6), .F(ou[7]));
  sub_ALU sub_alu_2 (
    .Ai(A[6]), .Cin(sub_alu_3_cout), .Bi(B[6]), .S1_S0(undriven), .S3_S2(S3_S2), .A_i1(A[7]), .A_i2(A[5]),
    .Cout(sub_alu_2_cout), .F(ou[6]));
  sub_ALU sub_alu_3 (
    .Ai(A[5]), .Cin(sub_alu_4_cout), .Bi(B[5]), .S1_S0(undriven), .S3_S2(S3_S2), .A_i1(A[6]), .A_i2(A[4]),
    .Cout(sub_alu_3_cout), .F(ou[5]));
  sub_ALU sub_alu_4 (
    .Ai(A[4]), .Cin(sub_alu_4_cout), .Bi(B[4]), .S1_S0(undriven), .S3_S2(S3_S2), .A_i1(A[5]), .A_i2(A[3]),
    .Cout(sub_alu_4_cout), .F(ou[4]));
  sub_ALU sub_alu_5 (
    .Ai(A[3]), .Cin(sub_alu_6_cout), .Bi(B[3]), .S1_S0(S1_S0), .S3_S2(S3_S2), .A_i1(A[4]), .A_i2(A[2]),
    .Cout(sub_alu_4_cout), .F(ou[3]));
  sub_ALU sub_alu_6 (
    .Ai(A[2]), .Cin(sub_alu_7_cout), .Bi(B[2]), .S1_S0(S1_S0), .S3_S2(S3_S2), .A_i1(A[3]), .A_i2(A[1]),
    .Cout(sub_alu_6_cout), .F(ou[2]));
  sub_ALU sub_alu_7 (
    .Ai(A[1]), .Cin(sub_alu_8_cout), .Bi(B[1]), .S1_S0(S1_S0), .S3_S2(S3_S2), .A_i1(A[2]), .A_i2(A[0]),
    .Cout(sub_alu_7_cout), .F(ou[1]));
  sub_ALU sub_alu_8 (
    .Ai(A[0]), .Cin(Cin), .Bi(B[0]), .S1_S0(S1_S0), .S3_S2(S3_S2), .A_i1(A[1]), .A_i2(1'b0),
    .Cout(sub_alu_8_cout), .F(ou[0]));
endmodule

module sub_ALU (
  input  Ai,
  input  Cin,
  input  Bi,
  input  [1:0] S1_S0,
  input  [1:0] S3_S2,
  input  A_i1,
  input  A_i2,
  output Cout,
  output F
);

  wire adder_1_out, and_1_out, multiplexer_1_out, multiplexer_2_out, not_1_out, not_2_out, or_1_out,
       xor_1_out;

  not not_1 (not_1_out, Ai);
  and and_1 (and_1_out, Ai, Bi);
  or or_1 (or_1_out, Ai, Bi);
  xor xor_1 (xor_1_out, Ai, Bi);
  not not_2 (not_2_out, Bi);
  Multiplexer #(.select(2)) multiplexer_1 (
    .in0(1'b0), .in1(Bi), .in2(not_2_out), .in3(1'b1), .out(multiplexer_1_out), .sel(S1_S0));
  Multiplexer #(.select(2)) multiplexer_2 (
    .in0(and_1_out), .in1(or_1_out), .in2(xor_1_out), .in3(not_1_out), .out(multiplexer_2_out), .sel(S1_S0));
  Adder #(.width(1)) adder_1 (.a(Ai), .b(multiplexer_1_out), .out(adder_1_out), .cin(Cin), .cout(Cout));
  Multiplexer #(.select(2)) multiplexer_3 (
    .in0(adder_1_out), .in1(multiplexer_2_out), .in2(A_i1), .in3(A_i2), .out(F), .sel(S3_S2));
endmodule

module ALU_new (
  input  [15:0] AC,
  input  [15:0] DR,
  input  [15:0] INPR,
  input  [2:0] ALUselect,
  input  IPLS,
  input  IPRS,
  output [15:0] ALUout,
  output Cout
);

  wire [15:0] adder_1_out, and_1_out, not_1_out;

  assign not_1_out = ~AC;  // NOT_Gate not_1, 16 bits wide
  Adder #(.width(16)) adder_1 (.a(AC), .b(DR), .out(adder_1_out), .cin(1'b0), .cout(Cout));
  assign and_1_out = AC & DR;  // AND_Gate and_1, 16 bits wide
  Multiplexer #(.select(3), .width(16)) multiplexer_1 (
    .in1(and_1_out), .in2(adder_1_out), .in3(DR), .in4(INPR), .in5(not_1_out), .in6({IPRS, AC[15:1]}),
    .in7({AC[14:0], IPLS}), .out(ALUout), .sel(ALUselect));  // open: in0
endmodule

module E_FF (
  input  E_ip,
  input  comE,
  input  load,
  input  clr,
  input  clk,
  output E_ff_out
);

  wire multiplexer_1_out, multiplexer_2_out, multiplexer_3_out, not_1_out;

  Multiplexer multiplexer_1 (.in0(E_ff_out), .in1(not_1_out), .out(multiplexer_1_out), .sel(comE));
  not not_1 (not_1_out, E_ff_out);
  Multiplexer multiplexer_2 (.in0(multiplexer_1_out), .in1(E_ip), .out(multiplexer_2_out), .sel(load));
  Multiplexer multiplexer_3 (.in0(multiplexer_2_out), .in1(1'b0), .out(multiplexer_3_out), .sel(clr));
  D_Flip_Flop d_ff_1 (.D(multiplexer_3_out), .clk(clk), .Q(E_ff_out));  // open: Qn, preset, reset
endmodule

module control_sequence_counter (
  input  INR_sc,
  input  CLR_sc,
  input  Decoder_en,
  input  clk,
  output [15:0] T0_15
);

  wire [3:0] adder_1_out, multiplexer_1_out, multiplexer_2_out, register_1_q;

  Adder #(.width(4)) adder_1 (.a(register_1_q), .b(4'b0001), .out(adder_1_out), .cin(1'b0));  // open: cout
  Multiplexer #(.width(4)) multiplexer_1 (.in0(register_1_q), .in1(adder_1_out), .out(multiplexer_1_out), .sel(INR_sc));
  Multiplexer #(.width(4)) multiplexer_2 (
    .in0(multiplexer_1_out), .in1(4'b0000), .out(multiplexer_2_out), .sel(CLR_sc));
  Register #(.width(4)) register_1 (.D(multiplexer_2_out), .clk(clk), .Q(register_1_q));  // open: en, clr
  Decoder #(.select(4)) decoder_1 (
    .out0(T0_15[0]), .out1(T0_15[1]), .out2(T0_15[2]), .out3(T0_15[3]), .out4(T0_15[4]), .out5(T0_15[5]),
    .out6(T0_15[6]), .out7(T0_15[7]), .out8(T0_15[8]), .out9(T0_15[9]), .out10(T0_15[10]), .out11(T0_15[11]),
    .out12(T0_15[12]), .out13(T0_15[13]), .out14(T0_15[14]), .out15(T0_15[15]), .sel(register_1_q),
    .en(Decoder_en));
endmodule

module integration (
  input  in_1,
  input  RST
);

  wire AC_15, ACEqI0, ACload, ADD, and_9_out, and_10_out, and_11_out, and_12_out, and_13_out, and_16_out,
       and_17_out, ANDop, ARload, BSA, BUN, clk, CLR_sc, D0, D1, D2, D3, D4, D5, D6, D7, DR, DREqI0, E_clr,
       Eop, I, INR_sc, IRload, n, not_1_out, not_2_out, not_3_out, not_4_out, or_1_out, or_15_out, p, PCclr,
       PCinr, r, rB0, rB1, rB2, rB3, rB4, rB5, rB6, rB7, rB8, rB9, rB10, rB11, rdEN, STA, T0, T1, T2, T3, T4,
       T5, T6, T7, w, wtEN, x1, x2, x3, x4, x5, x6, x7, y, z;
  wire [2:0] M2M1M0, S2S1S0;
  wire [14:0] AC_15_0;
  wire [15:0] datapath_1_ir_15_0, DR_15_0;

  Comparator #(.width(16)) comparator_1 (.a({16{1'b0}}), .b({AC_15, AC_15_0}), .eq(ACEqI0));  // open: gt, lt
  and and_1 (BUN, T4, D4);
  and and_2 (BSA, T5, D5);
  or or_1 (or_1_out, D0, D1, D2, D6);
  main2 main2_1 (
    .IR15_0(datapath_1_ir_15_0), .Cntrl(T2), .DcodrEN2(1'b1), .CLK1(clk), .INR_sc(INR_sc), .CLR_sc(CLR_sc),
    .Decoder_en(1'b1), .CLK2(clk), .I(I), .D7(D7), .D6(D6), .D5(D5), .D4(D4), .D3(D3), .D2(D2), .D1(D1),
    .D0(D0), .T0(T0), .T1(T1), .T2(T2), .T3(T3), .T4(T4), .T5(T5), .T6(T6), .T7(T7), .r(r), .rB11(rB11),
    .rB10(rB10), .rB9(rB9), .rB8(rB8), .rB7(rB7), .rB6(rB6), .rB5(rB5), .rB4(rB4), .rB3(rB3), .rB2(rB2),
    .rB1(rB1), .rB0(rB0));
  and and_3 (n, D5, T4);
  and and_4 (STA, D3, T4);
  and and_5 (DR, D2, T5);
  and and_6 (w, D6, T6);
  and and_7 (y, or_1_out, T4);
  or or_2 (wtEN, STA, n, w);
  Comparator #(.width(16)) comparator_2 (.a({16{1'b0}}), .b(DR_15_0), .eq(DREqI0));  // open: gt, lt
  or or_3 (x1, BUN, BSA);
  or or_4 (x2, T0, n);
  or or_5 (x7, T1, z, y);
  buf or_6 (x5, T2);  // OR_Gate
  buf or_7 (x4, STA);  // OR_Gate
  or or_8 (x3, DR, w);
  buf or_9 (E_clr, rB10);  // OR_Gate
  buf or_10 (IRload, T1);  // OR_Gate
  and and_8 (p, D7, I, T3);
  or or_11 (rdEN, T1, z, y);
  busSelectGen busselectgen_1 (.x1(x1), .x3(x3), .x5(x5), .x7(x7), .x2(x2), .x6(x6), .x4(x4), .S2S1S0(S2S1S0));
  and and_9 (and_9_out, D6, T5);
  not not_1 (not_1_out, AC_15);
  and and_10 (and_10_out, w, DREqI0);
  and and_11 (and_11_out, rB4, not_1_out);
  and and_12 (and_12_out, rB3, AC_15);
  and and_13 (and_13_out, rB2, ACEqI0);
  not not_2 (not_2_out, Eop);
  and and_14 (ADD, D1, T5);
  and and_15 (ANDop, D0, T5);
  not not_3 (not_3_out, rB0);
  Clock clock_1 (.out(clk));
  not not_4 (not_4_out, D7);
  dataPath datapath_1 (
    .wtEN(wtEN), .rdEN(rdEN), .ARinr(n), .ARload(ARload), .PCinr(PCinr), .PCload(x1), .PCclr(PCclr),
    .DRinr(and_9_out), .DRload(y), .S2S1S0(S2S1S0), .ACinr(rB5), .ACload(ACload), .ACclr(rB11), .comE(rB8),
    .Eload(ADD), .ALUselect(M2M1M0), .Eclr(rB10), .IRload(IRload), .DR_15_0(DR_15_0),
    .AC_15_0({AC_15, AC_15_0}), .Eop(Eop), .IR_15_0(datapath_1_ir_15_0));  // open: ARclr, DRclr, TRinr, TRload, TRclr
  and and_16 (and_16_out, rB1, not_2_out);
  and and_17 (and_17_out, not_3_out, INR_sc);
  and and_18 (z, not_4_out, I, T3);
  buf or_12 (PCclr, RST);  // OR_Gate
  or or_13 (PCinr, and_10_out, T1, and_11_out, and_12_out, and_13_out, and_16_out);
  or or_14 (ACload, ADD, rB9, rB7, rB6, DR, ANDop);
  busSelectGen busselectgen_2 (
    .x1(ANDop), .x3(DR), .x5(rB9), .x7(rB6), .x2(ADD), .x6(rB7), .S2S1S0(M2M1M0));  // open: x4
  or or_15 (or_15_out, in_1, and_17_out);
  or or_16 (ARload, T0, T2, z);
  or or_17 (CLR_sc, BUN, DR, r, ANDop, ADD, p, STA, w);
  D_Flip_Flop d_ff_1 (.D(or_15_out), .clk(clk), .Q(INR_sc));  // open: Qn, preset, reset

  // Other names for the same wires on the sheet: AC_15_0[15] = AC_15
endmodule

module main2 (
  input  [15:0] IR15_0,
  input  Cntrl,
  input  DcodrEN2,
  input  CLK1,
  input  INR_sc,
  input  CLR_sc,
  input  Decoder_en,
  input  CLK2,
  output I,
  output D7,
  output D6,
  output D5,
  output D4,
  output D3,
  output D2,
  output D1,
  output D0,
  output T0,
  output T1,
  output T2,
  output T3,
  output T4,
  output T5,
  output T6,
  output T7,
  output r,
  output rB11,
  output rB10,
  output rB9,
  output rB8,
  output rB7,
  output rB6,
  output rB5,
  output rB4,
  output rB3,
  output rB2,
  output rB1,
  output rB0
);

  wire multiplexer_1_out, not_1_out;
  wire [15:8] control_sequence_counter_1_t0_15;

  Multiplexer multiplexer_1 (.in0(I), .in1(IR15_0[15]), .out(multiplexer_1_out), .sel(Cntrl));
  D_Flip_Flop d_ff_1 (.D(multiplexer_1_out), .clk(CLK1), .Q(I));  // open: Qn, preset, reset
  control_sequence_counter control_sequence_counter_1 (
    .INR_sc(INR_sc), .CLR_sc(CLR_sc), .Decoder_en(Decoder_en), .clk(CLK2),
    .T0_15({control_sequence_counter_1_t0_15, T7, T6, T5, T4, T3, T2, T1, T0}));
  Decoder #(.select(3)) decoder_1 (
    .out0(D0), .out1(D1), .out2(D2), .out3(D3), .out4(D4), .out5(D5), .out6(D6), .out7(D7),
    .sel(IR15_0[14:12]), .en(DcodrEN2));
  not not_1 (not_1_out, I);
  and and_1 (r, D7, not_1_out, T3);
  and and_2 (rB11, r, IR15_0[11]);
  and and_3 (rB10, r, IR15_0[10]);
  and and_4 (rB9, r, IR15_0[9]);
  and and_5 (rB8, r, IR15_0[8]);
  and and_6 (rB7, r, IR15_0[7]);
  and and_7 (rB6, r, IR15_0[6]);
  and and_8 (rB5, r, IR15_0[5]);
  and and_9 (rB4, r, IR15_0[4]);
  and and_10 (rB3, r, IR15_0[3]);
  and and_11 (rB2, r, IR15_0[2]);
  and and_12 (rB1, r, IR15_0[1]);
  and and_13 (rB0, r, IR15_0[0]);

  // Other names for the same wires on the sheet: B0 = IR15_0[0]; B1 = IR15_0[1]; B2 = IR15_0[2]; B3 = IR15_0[3];
  //   B4 = IR15_0[4]; B5 = IR15_0[5]; B6 = IR15_0[6]; B7 = IR15_0[7]; B8 = IR15_0[8]; B9 = IR15_0[9];
  //   B10 = IR15_0[10]; B11 = IR15_0[11]
endmodule

module busSelectGen (
  input  x1,
  input  x3,
  input  x5,
  input  x7,
  input  x2,
  input  x6,
  input  x4,
  output [2:0] S2S1S0
);

  or or_1 (S2S1S0[0], x1, x3, x5, x7);
  or or_2 (S2S1S0[1], x7, x3, x2, x6);
  or or_3 (S2S1S0[2], x6, x5, x7, x4);
endmodule
